// Logisim project 16-bit-basic-computer-using-logic-gates.circ as structural Verilog: 26 circuits, main circuit main
module main (
  input  CLR,
  input  in_2,
  input  [11:0] in_3,
  input  en,
  input  CLK_FOR_E,
  input  [7:0] in_6,
  input  FGO,
  input  FGI,
  input  CLR_2,
  output [11:0] out_10,
  output [15:0] out_11,
  output E_CARRY,
  output R,
  output IEN,
  output [7:0] out_15
);

  wire AC_CONTROL_add, AC_CONTROL_and, AC_CONTROL_clr, AC_CONTROL_com, AC_CONTROL_dr, AC_CONTROL_inpr,
       AC_CONTROL_inr, AC_CONTROL_ld, AC_CONTROL_shl, AC_CONTROL_shr, and_1_out, and_2_out, and_3_out,
       and_4_out, ar_control_1_clr, ar_control_1_inr, ar_control_1_ld, clock_1_out, clock_2_out, clock_3_out,
       d_ff_1_q, d_ff_2_q, d_ff_3_q, d_ff_4_q, dr_control_1_inr, dr_control_1_ld, ir_drcoder_1_d7,
       ir_drcoder_1_i, memory_control_1_read, memory_control_1_write, multiplexer_1_out, multiplexer_2_out,
       not_1_out, not_2_out, not_3_out, not_4_out, not_5_out, not_6_out, p_out, pc_control_1_clr,
       pc_control_1_inr, pc_control_1_ld, r_out;
  wire [2:0] bus_control_1_s0;
  wire [6:0] ir_drcoder_1_d0, seq_counter_1_t0;
  wire [7:0] inpr__reg_1_o0;
  wire [11:0] ar_pc__load_reg_1_o0, bit_extender_1_out, ir_drcoder_1_ar;
  wire [15:0] bus_1_output, dr_ac_tr__load__reg_1_o0, dr_ac_tr__load__reg_3_o0, ir__reg_1_o0,
       n16bit_alu_1_ac_out, ram_1_data;

  and u_r (r_out, ir_drcoder_1_d7, not_1_out, seq_counter_1_t0[3]);
  Clock clock_1 (.out(clock_1_out));
  not not_1 (not_1_out, d_ff_3_q);
  and p (p_out, ir_drcoder_1_d7, d_ff_3_q, seq_counter_1_t0[3]);
  D_Flip_Flop d_ff_1 (.clk(clock_2_out), .D(FGO), .Q(d_ff_1_q), .reset(CLR_2));  // open: Qn, preset, en
  D_Flip_Flop d_ff_2 (.clk(clock_2_out), .D(FGI), .Q(d_ff_2_q), .reset(CLR_2));  // open: Qn, preset, en
  D_Flip_Flop d_ff_3 (.clk(clock_1_out), .D(ir_drcoder_1_i), .Q(d_ff_3_q));  // open: Qn, preset, en, reset
  not not_2 (not_2_out, d_ff_3_q);
  Clock clock_2 (.out(clock_2_out));
  IR_drcoder ir_drcoder_1 (
    .IR(ir__reg_1_o0), .D0(ir_drcoder_1_d0[0]), .D1(ir_drcoder_1_d0[1]), .D2(ir_drcoder_1_d0[2]),
    .D3(ir_drcoder_1_d0[3]), .D4(ir_drcoder_1_d0[4]), .D5(ir_drcoder_1_d0[5]), .D6(ir_drcoder_1_d0[6]),
    .D7(ir_drcoder_1_d7), .AR(ir_drcoder_1_ar), .I(ir_drcoder_1_i));
  IEN_control ien_control_1 (
    .p(clock_2_out), .B7(p_out), .Clock(ir_drcoder_1_ar[7]), .B6(ir_drcoder_1_ar[6]), .R(R),
    .T2(seq_counter_1_t0[2]), .IEN(IEN));
  IR__reg ir__reg_1 (
    .I0(bus_1_output[0]), .I1(bus_1_output[1]), .I2(bus_1_output[2]), .I3(bus_1_output[3]),
    .I4(bus_1_output[4]), .I5(bus_1_output[5]), .I6(bus_1_output[6]), .I7(bus_1_output[7]),
    .I8(bus_1_output[8]), .I9(bus_1_output[9]), .I10(bus_1_output[10]), .I11(bus_1_output[11]),
    .I12(bus_1_output[12]), .I13(bus_1_output[13]), .I14(bus_1_output[14]), .I15(bus_1_output[15]),
    .Load(and_2_out), .CLOCK(clock_3_out), .O0(ir__reg_1_o0[0]), .O1(ir__reg_1_o0[1]), .O2(ir__reg_1_o0[2]),
    .O3(ir__reg_1_o0[3]), .O4(ir__reg_1_o0[4]), .O5(ir__reg_1_o0[5]), .O6(ir__reg_1_o0[6]),
    .O7(ir__reg_1_o0[7]), .O8(ir__reg_1_o0[8]), .O9(ir__reg_1_o0[9]), .O10(ir__reg_1_o0[10]),
    .O11(ir__reg_1_o0[11]), .O12(ir__reg_1_o0[12]), .O13(ir__reg_1_o0[13]), .O14(ir__reg_1_o0[14]),
    .O15(ir__reg_1_o0[15]));
  R_control r_control_1 (
    .T0(seq_counter_1_t0[0]), .T1(seq_counter_1_t0[1]), .T2(seq_counter_1_t0[2]), .IEN(IEN), .FGI(d_ff_2_q),
    .FGO(d_ff_1_q), .R(R), .Clock(clock_2_out), .R_2(R));
  and and_1 (and_1_out, ir_drcoder_1_ar[0], r_out);
  not not_3 (not_3_out, and_1_out);
  D_Flip_Flop d_ff_4 (.clk(clock_3_out), .D(not_3_out), .Q(d_ff_4_q));  // open: Qn, preset, en, reset
  not not_4 (not_4_out, R);
  SEQ_counter seq_counter_1 (
    .incr(d_ff_4_q), .CLOCK(clock_3_out), .CLEAR(CLR), .T0(seq_counter_1_t0[0]), .T1(seq_counter_1_t0[1]),
    .T2(seq_counter_1_t0[2]), .T3(seq_counter_1_t0[3]), .T4(seq_counter_1_t0[4]), .T5(seq_counter_1_t0[5]),
    .T6(seq_counter_1_t0[6]));  // open: T7
  not not_5 (not_5_out, ir_drcoder_1_d7);
  memory_control memory_control_1 (
    .D0(ir_drcoder_1_d0[0]), .D1(ir_drcoder_1_d0[1]), .D2(ir_drcoder_1_d0[2]), .D3(ir_drcoder_1_d0[3]),
    .D4(ir_drcoder_1_d0[4]), .D5(ir_drcoder_1_d0[5]), .D6(ir_drcoder_1_d0[6]), .D7(ir_drcoder_1_d7),
    .I(d_ff_3_q), .R(R), .T1(seq_counter_1_t0[1]), .T4(seq_counter_1_t0[4]), .T3(seq_counter_1_t0[3]),
    .T6(seq_counter_1_t0[6]), .Write(memory_control_1_write), .Read(memory_control_1_read));
  and and_2 (and_2_out, not_4_out, seq_counter_1_t0[1]);
  and and_3 (and_3_out, R, seq_counter_1_t0[0]);
  and and_4 (and_4_out, ir_drcoder_1_ar[10], p_out);
  not not_6 (not_6_out, R);
  AR_control ar_control_1 (
    .D_prime_7(not_5_out), .I(d_ff_3_q), .T3(seq_counter_1_t0[3]), .T2(seq_counter_1_t0[2]), .R(R),
    .T0(seq_counter_1_t0[0]), .D5(ir_drcoder_1_d0[5]), .T4(seq_counter_1_t0[4]), .LD(ar_control_1_ld),
    .INR(ar_control_1_inr), .CLR(ar_control_1_clr));
  pc_control pc_control_1 (
    .D4(ir_drcoder_1_d0[4]), .T4(seq_counter_1_t0[4]), .D5(ir_drcoder_1_d0[5]), .T5(seq_counter_1_t0[5]),
    .R_prime(not_4_out), .T1(seq_counter_1_t0[1]), .R(R), .T2(seq_counter_1_t0[2]), .D6(ir_drcoder_1_d0[6]),
    .T6(seq_counter_1_t0[6]), .r_2(r_out), .B4(ir_drcoder_1_ar[4]), .B3(ir_drcoder_1_ar[3]),
    .B2(ir_drcoder_1_ar[2]), .B1(ir_drcoder_1_ar[1]), .P(p_out), .B9(ir_drcoder_1_ar[9]),
    .B8(ir_drcoder_1_ar[8]), .R_3(R), .T1_2(seq_counter_1_t0[1]), .LD(pc_control_1_ld),
    .INR(pc_control_1_inr), .CLR(pc_control_1_clr));
  AC_control AC_CONTROL (
    .D0(ir_drcoder_1_d0[0]), .T5(seq_counter_1_t0[5]), .D1(ir_drcoder_1_d0[1]), .D2(ir_drcoder_1_d0[2]),
    .T5_2(seq_counter_1_t0[5]), .P(p_out), .B11(ir_drcoder_1_ar[11]), .r(r_out), .B9(ir_drcoder_1_ar[9]),
    .B7(ir_drcoder_1_ar[7]), .B6(ir_drcoder_1_ar[6]), .B5(ir_drcoder_1_ar[5]), .B11_2(ir_drcoder_1_ar[11]),
    .AND(AC_CONTROL_and), .ADD(AC_CONTROL_add), .DR(AC_CONTROL_dr), .INPR(AC_CONTROL_inpr),
    .COM(AC_CONTROL_com), .SHR(AC_CONTROL_shr), .SHL(AC_CONTROL_shl), .LD(AC_CONTROL_ld),
    .INR(AC_CONTROL_inr), .CLR(AC_CONTROL_clr));
  bus_control bus_control_1 (
    .D0_D6(ir_drcoder_1_d0), .D7_prime(not_5_out), .T0(seq_counter_1_t0[0]), .T1(seq_counter_1_t0[1]),
    .T2(seq_counter_1_t0[2]), .T3(seq_counter_1_t0[3]), .T4(seq_counter_1_t0[4]), .T5(seq_counter_1_t0[5]),
    .T6(seq_counter_1_t0[6]), .R(R), .R_prime(not_6_out), .I(d_ff_3_q), .p(p_out), .B10(ir_drcoder_1_ar[10]),
    .S2(bus_control_1_s0[2]), .S1(bus_control_1_s0[1]), .S0(bus_control_1_s0[0]));
  Bit_Extender #(.in_width(16), .out_width(12)) bit_extender_1 (.in(bus_1_output), .out(bit_extender_1_out));
  Multiplexer #(.enable("false")) multiplexer_1 (.in0(pc_control_1_ld), .in1(1'b1), .out(multiplexer_1_out), .sel(en));
  DR_control dr_control_1 (
    .D0(ir_drcoder_1_d0[0]), .T4(seq_counter_1_t0[4]), .D1(ir_drcoder_1_d0[1]), .D2(ir_drcoder_1_d0[2]),
    .D6(ir_drcoder_1_d0[6]), .T5(seq_counter_1_t0[5]), .LD(dr_control_1_ld), .INR(dr_control_1_inr));
  _16bit_ALU u_16bit_alu_1 (
    .AC_IN(out_11), .DR_IN(dr_ac_tr__load__reg_1_o0), .AND(AC_CONTROL_and), .ADD(AC_CONTROL_add),
    .DR(AC_CONTROL_dr), .IN(AC_CONTROL_inpr), .COMP(AC_CONTROL_com), .SHR(AC_CONTROL_shr),
    .SHL(AC_CONTROL_shl), .INPR(inpr__reg_1_o0), .clock_for_E(CLK_FOR_E), .LD(1'b1),
    .ac_out(n16bit_alu_1_ac_out), .E_carry(E_CARRY));
  INPR__reg inpr__reg_1 (
    .I0(in_6[0]), .I1(in_6[1]), .I2(in_6[2]), .I3(in_6[3]), .I4(in_6[4]), .I5(in_6[5]), .I6(in_6[6]),
    .I7(in_6[7]), .CLOCK(clock_3_out), .O0(inpr__reg_1_o0[0]), .O1(inpr__reg_1_o0[1]),
    .O2(inpr__reg_1_o0[2]), .O3(inpr__reg_1_o0[3]), .O4(inpr__reg_1_o0[4]), .O5(inpr__reg_1_o0[5]),
    .O6(inpr__reg_1_o0[6]), .O7(inpr__reg_1_o0[7]));
  RAM #(.addrWidth(12), .dataWidth(16), .bus("separate")) ram_1 (
    .addr(ar_pc__load_reg_1_o0), .din(bus_1_output), .data(ram_1_data), .str(memory_control_1_write),
    .clk(clock_3_out), .ld(memory_control_1_read));  // open: sel, clr
  AR_PC__load_reg ar_pc__load_reg_1 (
    .I0(bus_1_output[0]), .I1(bus_1_output[1]), .I2(bus_1_output[2]), .I3(bus_1_output[3]),
    .I4(bus_1_output[4]), .I5(bus_1_output[5]), .I6(bus_1_output[6]), .I7(bus_1_output[7]),
    .I8(bus_1_output[8]), .I9(bus_1_output[9]), .I10(bus_1_output[10]), .I11(bus_1_output[11]),
    .Load(ar_control_1_ld), .INC(ar_control_1_inr), .CLOCK(clock_3_out), .CLR(ar_control_1_clr),
    .O0(ar_pc__load_reg_1_o0[0]), .O1(ar_pc__load_reg_1_o0[1]), .O2(ar_pc__load_reg_1_o0[2]),
    .O3(ar_pc__load_reg_1_o0[3]), .O4(ar_pc__load_reg_1_o0[4]), .O5(ar_pc__load_reg_1_o0[5]),
    .O6(ar_pc__load_reg_1_o0[6]), .O7(ar_pc__load_reg_1_o0[7]), .O8(ar_pc__load_reg_1_o0[8]),
    .O9(ar_pc__load_reg_1_o0[9]), .O10(ar_pc__load_reg_1_o0[10]), .O11(ar_pc__load_reg_1_o0[11]));
  OUTR__load_reg outr__load_reg_1 (
    .I0(bus_1_output[0]), .I1(bus_1_output[1]), .I2(bus_1_output[2]), .I3(bus_1_output[3]),
    .I4(bus_1_output[4]), .I5(bus_1_output[5]), .I6(bus_1_output[6]), .I7(bus_1_output[7]), .Load(and_4_out),
    .CLOCK(clock_3_out), .O0(out_15[0]), .O1(out_15[1]), .O2(out_15[2]), .O3(out_15[3]), .O4(out_15[4]),
    .O5(out_15[5]), .O6(out_15[6]), .O7(out_15[7]));
  pc pc_1 (
    .\input (bit_extender_1_out), .in_5(in_3), .En(en), .Load(multiplexer_1_out), .INC(pc_control_1_inr),
    .CLOCK(multiplexer_2_out), .CLR(pc_control_1_clr), .O0(out_10[0]), .O1(out_10[1]), .O2(out_10[2]),
    .O3(out_10[3]), .O4(out_10[4]), .O5(out_10[5]), .O6(out_10[6]), .O7(out_10[7]), .O8(out_10[8]),
    .O9(out_10[9]), .O10(out_10[10]), .O11(out_10[11]));
  DR_AC_TR__load__reg dr_ac_tr__load__reg_1 (
    .I0(bus_1_output[0]), .I1(bus_1_output[1]), .I2(bus_1_output[2]), .I3(bus_1_output[3]),
    .I4(bus_1_output[4]), .I5(bus_1_output[5]), .I6(bus_1_output[6]), .I7(bus_1_output[7]),
    .I8(bus_1_output[8]), .I9(bus_1_output[9]), .I10(bus_1_output[10]), .I11(bus_1_output[11]),
    .I12(bus_1_output[12]), .I13(bus_1_output[13]), .I14(bus_1_output[14]), .I15(bus_1_output[15]),
    .Load(dr_control_1_ld), .INC(dr_control_1_inr), .CLOCK(clock_3_out), .O0(dr_ac_tr__load__reg_1_o0[0]),
    .O1(dr_ac_tr__load__reg_1_o0[1]), .O2(dr_ac_tr__load__reg_1_o0[2]), .O3(dr_ac_tr__load__reg_1_o0[3]),
    .O4(dr_ac_tr__load__reg_1_o0[4]), .O5(dr_ac_tr__load__reg_1_o0[5]), .O6(dr_ac_tr__load__reg_1_o0[6]),
    .O7(dr_ac_tr__load__reg_1_o0[7]), .O8(dr_ac_tr__load__reg_1_o0[8]), .O9(dr_ac_tr__load__reg_1_o0[9]),
    .O10(dr_ac_tr__load__reg_1_o0[10]), .O11(dr_ac_tr__load__reg_1_o0[11]),
    .O12(dr_ac_tr__load__reg_1_o0[12]), .O13(dr_ac_tr__load__reg_1_o0[13]),
    .O14(dr_ac_tr__load__reg_1_o0[14]), .O15(dr_ac_tr__load__reg_1_o0[15]));  // open: CLR
  DR_AC_TR__load__reg dr_ac_tr__load__reg_2 (
    .I0(n16bit_alu_1_ac_out[0]), .I1(n16bit_alu_1_ac_out[1]), .I2(n16bit_alu_1_ac_out[2]),
    .I3(n16bit_alu_1_ac_out[3]), .I4(n16bit_alu_1_ac_out[4]), .I5(n16bit_alu_1_ac_out[5]),
    .I6(n16bit_alu_1_ac_out[6]), .I7(n16bit_alu_1_ac_out[7]), .I8(n16bit_alu_1_ac_out[8]),
    .I9(n16bit_alu_1_ac_out[9]), .I10(n16bit_alu_1_ac_out[10]), .I11(n16bit_alu_1_ac_out[11]),
    .I12(n16bit_alu_1_ac_out[12]), .I13(n16bit_alu_1_ac_out[13]), .I14(n16bit_alu_1_ac_out[14]),
    .I15(n16bit_alu_1_ac_out[15]), .Load(AC_CONTROL_ld), .INC(AC_CONTROL_inr), .CLOCK(clock_3_out),
    .CLR(AC_CONTROL_clr), .O0(out_11[0]), .O1(out_11[1]), .O2(out_11[2]), .O3(out_11[3]), .O4(out_11[4]),
    .O5(out_11[5]), .O6(out_11[6]), .O7(out_11[7]), .O8(out_11[8]), .O9(out_11[9]), .O10(out_11[10]),
    .O11(out_11[11]), .O12(out_11[12]), .O13(out_11[13]), .O14(out_11[14]), .O15(out_11[15]));
  DR_AC_TR__load__reg dr_ac_tr__load__reg_3 (
    .I0(bus_1_output[0]), .I1(bus_1_output[1]), .I2(bus_1_output[2]), .I3(bus_1_output[3]),
    .I4(bus_1_output[4]), .I5(bus_1_output[5]), .I6(bus_1_output[6]), .I7(bus_1_output[7]),
    .I8(bus_1_output[8]), .I9(bus_1_output[9]), .I10(bus_1_output[10]), .I11(bus_1_output[11]),
    .I12(bus_1_output[12]), .I13(bus_1_output[13]), .I14(bus_1_output[14]), .I15(bus_1_output[15]),
    .Load(and_3_out), .CLOCK(clock_3_out), .O0(dr_ac_tr__load__reg_3_o0[0]),
    .O1(dr_ac_tr__load__reg_3_o0[1]), .O2(dr_ac_tr__load__reg_3_o0[2]), .O3(dr_ac_tr__load__reg_3_o0[3]),
    .O4(dr_ac_tr__load__reg_3_o0[4]), .O5(dr_ac_tr__load__reg_3_o0[5]), .O6(dr_ac_tr__load__reg_3_o0[6]),
    .O7(dr_ac_tr__load__reg_3_o0[7]), .O8(dr_ac_tr__load__reg_3_o0[8]), .O9(dr_ac_tr__load__reg_3_o0[9]),
    .O10(dr_ac_tr__load__reg_3_o0[10]), .O11(dr_ac_tr__load__reg_3_o0[11]),
    .O12(dr_ac_tr__load__reg_3_o0[12]), .O13(dr_ac_tr__load__reg_3_o0[13]),
    .O14(dr_ac_tr__load__reg_3_o0[14]), .O15(dr_ac_tr__load__reg_3_o0[15]));  // open: INC, CLR
  Clock clock_3 (.out(clock_3_out));
  BUS bus_1 (
    .selection(bus_control_1_s0), ._001(ar_pc__load_reg_1_o0), ._010(out_10),
    ._011(dr_ac_tr__load__reg_1_o0), ._100(out_11), ._101(ir__reg_1_o0), ._110(dr_ac_tr__load__reg_3_o0),
    ._111(ram_1_data), .\output (bus_1_output));
  DotMatrix #(.matrixcols(1), .matrixrows(12)) dotmatrix_1 (.col0(out_10));
  Multiplexer #(.enable("false")) multiplexer_2 (.in0(clock_3_out), .in1(in_2), .out(multiplexer_2_out), .sel(en));
  DotMatrix #(.matrixcols(1), .matrixrows(8)) dotmatrix_2 (.col0(out_15));
  DotMatrix #(.matrixcols(1), .matrixrows(16)) dotmatrix_3 (.col0(out_11));

  // Notes on the sheet:
  //   DECODER
  //   IR
  //   R CONTROL
  //   IEN CONTROL
  //   SEQ COUNTER
  //   MEMORY CONTROL
  //   AR CONTROL
  //   AC CONTROL
  //   PC CONTROL
  //   BUS CONTROL
  //   AR
  //   DR CONTROL
  //   ALU
  //   PC
  //   INRT
  //   TR
  //   OUTR
  //   DR
  //   AC
  //   BUS
  //   clock cycle
  //   AC OUTPUT
endmodule

module pc (
  input  Load,
  input  INC,
  input  [11:0] \input ,
  input  En,
  input  [11:0] in_5,
  input  CLOCK,
  input  CLR,
  output O0,
  output O1,
  output O2,
  output O3,
  output O4,
  output O5,
  output O6,
  output O7,
  output O8,
  output O9,
  output O10,
  output O11
);

  wire and_1_out, and_2_out, and_3_out, and_4_out, and_5_out, and_6_out, and_7_out, and_8_out, and_9_out,
       and_10_out, and_11_out, and_12_out, and_13_out, and_14_out, and_15_out, and_16_out, and_17_out,
       and_18_out, and_19_out, and_20_out, and_21_out, and_22_out, and_23_out, and_24_out, and_25_out,
       and_26_out, and_27_out, and_28_out, and_29_out, and_30_out, and_31_out, and_32_out, and_33_out,
       and_34_out, and_35_out, and_36_out, not_1_out, not_2_out, not_3_out, not_4_out, not_5_out, not_6_out,
       not_7_out, not_8_out, not_9_out, not_10_out, not_11_out, not_12_out, not_13_out, or_1_out, or_2_out,
       or_3_out, or_4_out, or_5_out, or_6_out, or_7_out, or_8_out, or_9_out, or_10_out, or_11_out, or_12_out,
       or_13_out, or_14_out, or_15_out, or_16_out, or_17_out, or_18_out, or_19_out, or_20_out, or_21_out,
       or_22_out, or_23_out, or_24_out;
  wire [11:0] multiplexer_1_out;

  Multiplexer #(.width(12), .enable("false")) multiplexer_1 (
    .in0(\input ), .in1(in_5), .out(multiplexer_1_out), .sel(En));
  not not_1 (not_1_out, Load);
  not not_2 (not_2_out, multiplexer_1_out[0]);
  not not_3 (not_3_out, multiplexer_1_out[1]);
  not not_4 (not_4_out, multiplexer_1_out[2]);
  not not_5 (not_5_out, multiplexer_1_out[3]);
  not not_6 (not_6_out, multiplexer_1_out[4]);
  not not_7 (not_7_out, multiplexer_1_out[5]);
  not not_8 (not_8_out, multiplexer_1_out[6]);
  not not_9 (not_9_out, multiplexer_1_out[7]);
  not not_10 (not_10_out, multiplexer_1_out[8]);
  not not_11 (not_11_out, multiplexer_1_out[9]);
  not not_12 (not_12_out, multiplexer_1_out[10]);
  not not_13 (not_13_out, multiplexer_1_out[11]);
  and and_1 (and_1_out, not_1_out, INC);
  and and_2 (and_2_out, Load, multiplexer_1_out[0]);
  and and_3 (and_3_out, Load, not_2_out);
  and and_4 (and_4_out, Load, multiplexer_1_out[1]);
  and and_5 (and_5_out, and_1_out, O0);
  and and_6 (and_6_out, Load, not_3_out);
  and and_7 (and_7_out, Load, multiplexer_1_out[2]);
  and and_8 (and_8_out, and_5_out, O1);
  and and_9 (and_9_out, Load, not_4_out);
  and and_10 (and_10_out, Load, multiplexer_1_out[3]);
  and and_11 (and_11_out, and_8_out, O2);
  and and_12 (and_12_out, Load, not_5_out);
  and and_13 (and_13_out, Load, multiplexer_1_out[4]);
  and and_14 (and_14_out, and_11_out, O3);
  and and_15 (and_15_out, Load, not_6_out);
  and and_16 (and_16_out, Load, multiplexer_1_out[5]);
  and and_17 (and_17_out, Load, not_7_out);
  and and_18 (and_18_out, Load, multiplexer_1_out[6]);
  and and_19 (and_19_out, Load, not_8_out);
  and and_20 (and_20_out, Load, multiplexer_1_out[7]);
  and and_21 (and_21_out, Load, not_9_out);
  and and_22 (and_22_out, Load, multiplexer_1_out[8]);
  and and_23 (and_23_out, Load, not_10_out);
  and and_24 (and_24_out, Load, multiplexer_1_out[9]);
  and and_25 (and_25_out, Load, not_11_out);
  and and_26 (and_26_out, Load, multiplexer_1_out[10]);
  and and_27 (and_27_out, and_36_out, O9);
  and and_28 (and_28_out, Load, not_12_out);
  and and_29 (and_29_out, Load, multiplexer_1_out[11]);
  and and_30 (and_30_out, and_27_out, O10);
  and and_31 (and_31_out, Load, not_13_out);
  and and_32 (and_32_out, and_14_out, O4);
  and and_33 (and_33_out, and_32_out, O5);
  and and_34 (and_34_out, and_33_out, O6);
  and and_35 (and_35_out, and_34_out, O7);
  and and_36 (and_36_out, and_35_out, O8);
  or or_1 (or_1_out, and_1_out, and_2_out);
  or or_2 (or_2_out, and_1_out, and_3_out);
  or or_3 (or_3_out, and_5_out, and_4_out);
  or or_4 (or_4_out, and_5_out, and_6_out);
  or or_5 (or_5_out, and_8_out, and_7_out);
  or or_6 (or_6_out, and_8_out, and_9_out);
  or or_7 (or_7_out, and_11_out, and_10_out);
  or or_8 (or_8_out, and_11_out, and_12_out);
  or or_9 (or_9_out, and_14_out, and_13_out);
  or or_10 (or_10_out, and_14_out, and_15_out);
  or or_11 (or_11_out, and_32_out, and_16_out);
  or or_12 (or_12_out, and_32_out, and_17_out);
  or or_13 (or_13_out, and_33_out, and_18_out);
  or or_14 (or_14_out, and_33_out, and_19_out);
  or or_15 (or_15_out, and_34_out, and_20_out);
  or or_16 (or_16_out, and_34_out, and_21_out);
  or or_17 (or_17_out, and_35_out, and_22_out);
  or or_18 (or_18_out, and_35_out, and_23_out);
  or or_19 (or_19_out, and_36_out, and_24_out);
  or or_20 (or_20_out, and_36_out, and_25_out);
  or or_21 (or_21_out, and_27_out, and_26_out);
  or or_22 (or_22_out, and_27_out, and_28_out);
  or or_23 (or_23_out, and_30_out, and_29_out);
  or or_24 (or_24_out, and_30_out, and_31_out);
  J_K_Flip_Flop j_k_ff_1 (.J(or_1_out), .clk(CLOCK), .K(or_2_out), .Q(O0), .reset(CLR));  // open: Qn, preset, en
  J_K_Flip_Flop j_k_ff_2 (.J(or_3_out), .clk(CLOCK), .K(or_4_out), .Q(O1), .reset(CLR));  // open: Qn, preset, en
  J_K_Flip_Flop j_k_ff_3 (.J(or_5_out), .clk(CLOCK), .K(or_6_out), .Q(O2), .reset(CLR));  // open: Qn, preset, en
  J_K_Flip_Flop j_k_ff_4 (.J(or_7_out), .clk(CLOCK), .K(or_8_out), .Q(O3), .reset(CLR));  // open: Qn, preset, en
  J_K_Flip_Flop j_k_ff_5 (.J(or_9_out), .clk(CLOCK), .K(or_10_out), .Q(O4), .reset(CLR));  // open: Qn, preset, en
  J_K_Flip_Flop j_k_ff_6 (.J(or_11_out), .clk(CLOCK), .K(or_12_out), .Q(O5), .reset(CLR));  // open: Qn, preset, en
  J_K_Flip_Flop j_k_ff_7 (.J(or_13_out), .clk(CLOCK), .K(or_14_out), .Q(O6), .reset(CLR));  // open: Qn, preset, en
  J_K_Flip_Flop j_k_ff_8 (.J(or_15_out), .clk(CLOCK), .K(or_16_out), .Q(O7), .reset(CLR));  // open: Qn, preset, en
  J_K_Flip_Flop j_k_ff_9 (.J(or_17_out), .clk(CLOCK), .K(or_18_out), .Q(O8), .reset(CLR));  // open: Qn, preset, en
  J_K_Flip_Flop j_k_ff_10 (.J(or_19_out), .clk(CLOCK), .K(or_20_out), .Q(O9), .reset(CLR));  // open: Qn, preset, en
  J_K_Flip_Flop j_k_ff_11 (.J(or_21_out), .clk(CLOCK), .K(or_22_out), .Q(O10), .reset(CLR));  // open: Qn, preset, en
  J_K_Flip_Flop j_k_ff_12 (.J(or_23_out), .clk(CLOCK), .K(or_24_out), .Q(O11), .reset(CLR));  // open: Qn, preset, en
endmodule

module x1_x7 (
  input  X1,
  input  X2,
  input  X3,
  input  X4,
  input  X5,
  input  X6,
  input  X7,
  output S2,
  output S1,
  output S0
);

  or or_1 (S2, X4, X5, X6, X7, X7);
  or or_2 (S1, X2, X3, X6, X6, X7);
  or or_3 (S0, X1, X3, X7, X5, X5);
endmodule

module bus_control (
  input  [6:0] D0_D6,
  input  D7_prime,
  input  T0,
  input  T1,
  input  T2,
  input  T3,
  input  T4,
  input  T5,
  input  T6,
  input  R,
  input  R_prime,
  input  I,
  input  p,
  input  B10,
  output S2,
  output S1,
  output S0
);

  wire and_1_out, and_2_out, and_3_out, and_4_out, and_5_out, and_6_out, and_7_out, and_8_out, and_9_out,
       and_10_out, and_11_out, and_12_out, and_13_out, and_14_out, or_1_out, or_2_out, or_3_out, or_4_out,
       or_5_out, or_6_out;

  and and_1 (and_1_out, D0_D6[4], T4);
  and and_2 (and_2_out, D0_D6[5], T5);
  and and_3 (and_3_out, R_prime, T0);
  and and_4 (and_4_out, R, T0);
  and and_5 (and_5_out, D0_D6[5], T4);
  and and_6 (and_6_out, D0_D6[2], T5);
  and and_7 (and_7_out, T6, D0_D6[6]);
  and and_8 (and_8_out, T4, D0_D6[3]);
  and and_9 (and_9_out, R_prime, T2);
  and and_10 (and_10_out, R, T1);
  and and_11 (and_11_out, p, B10);
  or or_1 (or_1_out, D0_D6[0], D0_D6[1], D0_D6[2], D0_D6[6]);
  or or_2 (or_2_out, and_1_out, and_2_out);
  or or_3 (or_3_out, and_3_out, and_4_out, and_5_out);
  or or_4 (or_4_out, and_6_out, and_7_out);
  or or_5 (or_5_out, and_11_out, and_8_out);
  and and_12 (and_12_out, or_1_out, T4);
  and and_13 (and_13_out, D7_prime, I, T3);
  and and_14 (and_14_out, R_prime, T1);
  or or_6 (or_6_out, and_12_out, and_13_out, and_14_out);
  x1_x7 x1_x7_1 (
    .X1(or_2_out), .X2(or_3_out), .X3(or_4_out), .X4(or_5_out), .X5(and_9_out), .X6(and_10_out),
    .X7(or_6_out), .S2(S2), .S1(S1), .S0(S0));
endmodule

module s2s1s0_decoder (
  input  _0,
  input  _1,
  input  _2,
  output out_4,
  output out_5,
  output out_6,
  output out_7,
  output out_8,
  output out_9,
  output out_10,
  output out_11
);

  Decoder #(.select(3)) decoder_1 (
    .out0(out_4), .out1(out_5), .out2(out_6), .out3(out_7), .out4(out_8), .out5(out_9), .out6(out_10),
    .out7(out_11), .sel({_2, _1, _0}));  // open: en
endmodule

module SEQ_counter (
  input  incr,
  input  CLOCK,
  input  CLEAR,
  output T0,
  output T1,
  output T2,
  output T3,
  output T4,
  output T5,
  output T6,
  output T7
);

  wire and_1_out, and_2_out, and_3_out, and_4_out, and_5_out, and_6_out, and_7_out, and_8_out, and_9_out,
       j_k_ff_1_q, j_k_ff_2_q, j_k_ff_3_q, not_1_out, not_2_out, not_3_out, not_4_out, or_1_out, or_2_out,
       or_3_out, or_4_out, or_5_out, or_6_out;

  not not_1 (not_1_out, 1'b0);
  not not_2 (not_2_out, 1'b0);
  not not_3 (not_3_out, 1'b0);
  not not_4 (not_4_out, 1'b0);
  and and_1 (and_1_out, not_4_out, incr);
  and and_2 (and_2_out, 1'b0, 1'b0);
  and and_3 (and_3_out, 1'b0, not_1_out);
  and and_4 (and_4_out, 1'b0, 1'b0);
  and and_5 (and_5_out, and_1_out, j_k_ff_1_q);
  and and_6 (and_6_out, 1'b0, not_2_out);
  and and_7 (and_7_out, 1'b0, 1'b0);
  and and_8 (and_8_out, 1'b0, not_3_out);
  and and_9 (and_9_out, and_5_out, j_k_ff_2_q);
  or or_1 (or_1_out, and_1_out, and_2_out);
  or or_2 (or_2_out, and_1_out, and_3_out);
  or or_3 (or_3_out, and_5_out, and_4_out);
  or or_4 (or_4_out, and_5_out, and_6_out);
  or or_5 (or_5_out, and_9_out, and_7_out);
  or or_6 (or_6_out, and_9_out, and_8_out);
  J_K_Flip_Flop j_k_ff_1 (
    .J(or_1_out), .clk(CLOCK), .K(or_2_out), .Q(j_k_ff_1_q), .reset(CLEAR));  // open: Qn, preset, en
  J_K_Flip_Flop j_k_ff_2 (
    .J(or_3_out), .clk(CLOCK), .K(or_4_out), .Q(j_k_ff_2_q), .reset(CLEAR));  // open: Qn, preset, en
  J_K_Flip_Flop j_k_ff_3 (
    .J(or_5_out), .clk(CLOCK), .K(or_6_out), .Q(j_k_ff_3_q), .reset(CLEAR));  // open: Qn, preset, en
  s2s1s0_decoder s2s1s0_decoder_1 (
    ._0(j_k_ff_1_q), ._1(j_k_ff_2_q), ._2(j_k_ff_3_q), .out_4(T0), .out_5(T1), .out_6(T2), .out_7(T3),
    .out_8(T4), .out_9(T5), .out_10(T6), .out_11(T7));
endmodule

module AC_control (
  input  D0,
  input  T5,
  input  D1,
  input  D2,
  input  T5_2,
  input  P,
  input  B11,
  input  r,
  input  B9,
  input  B7,
  input  B6,
  input  B5,
  input  B11_2,
  output AND,
  output ADD,
  output DR,
  output INPR,
  output COM,
  output LD,
  output SHR,
  output SHL,
  output INR,
  output CLR
);

  and and_1 (AND, D0, T5);
  and and_2 (ADD, D1, T5);
  and and_3 (DR, D2, T5_2);
  and and_4 (INPR, P, B11);
  and and_5 (COM, r, B9);
  and and_6 (SHR, r, B7);
  and and_7 (SHL, r, B6);
  and and_8 (INR, r, B5);
  and and_9 (CLR, r, B11_2);
  or or_1 (LD, AND, ADD, DR, INPR, COM, SHR, SHL);
endmodule

module _1bit_ALU (
  input  AND,
  input  ADD,
  input  DR,
  input  INP,
  input  COM,
  input  SHR,
  input  SHL,
  input  LD,
  input  AC0,
  input  DR_i,
  input  previous_in,
  input  inpr_i,
  input  AC_i_1,
  input  AC_i_1_2,
  output cout,
  output Output
);

  wire adder_1_out, and_1_out, and_2_out, and_3_out, and_4_out, and_5_out, and_6_out, and_7_out, not_1_out,
       or_1_out;

  Adder #(.width(1)) adder_1 (.a(AC0), .b(DR_i), .out(adder_1_out), .cin(previous_in), .cout(cout));
  not not_1 (not_1_out, AC0);
  and and_1 (and_1_out, AND, AC0, DR_i);
  and and_2 (and_2_out, ADD, adder_1_out);
  and and_3 (and_3_out, DR_i, DR);
  and and_4 (and_4_out, INP, inpr_i);
  and and_5 (and_5_out, not_1_out, COM);
  and and_6 (and_6_out, AC_i_1, SHR);
  and and_7 (and_7_out, SHL, AC_i_1_2);
  or or_1 (or_1_out, and_1_out, and_2_out, and_3_out, and_4_out, and_5_out, and_6_out, and_7_out);
  and and_8 (Output, LD, or_1_out);
endmodule

module _2bit_ALU (
  input  COMP,
  input  SHR,
  input  SHL,
  input  DR,
  input  INP,
  input  ADD,
  input  AND,
  input  AC0_IN,
  input  AC1_IN,
  input  DR0_IN,
  input  DR1_IN,
  input  PREVIOUS_IN,
  input  INPR0,
  input  INPR1,
  input  LD,
  input  E,
  input  ACI_1,
  output AC0_OUT,
  output AC1_OUT,
  output cout
);

  wire n1bit_alu_1_cout;

  _1bit_ALU u_1bit_alu_1 (
    .AC0(AC0_IN), .DR_i(DR0_IN), .previous_in(PREVIOUS_IN), .inpr_i(INPR0), .AC_i_1(AC1_IN), .AC_i_1_2(E),
    .AND(AND), .ADD(ADD), .DR(DR), .INP(INP), .COM(COMP), .SHR(SHR), .SHL(SHL), .cout(n1bit_alu_1_cout),
    .LD(LD), .Output(AC0_OUT));
  _1bit_ALU u_1bit_alu_2 (
    .AC0(AC1_IN), .DR_i(DR1_IN), .previous_in(n1bit_alu_1_cout), .inpr_i(INPR1), .AC_i_1(ACI_1),
    .AC_i_1_2(AC0_IN), .AND(AND), .ADD(ADD), .DR(DR), .INP(INP), .COM(COMP), .SHR(SHR), .SHL(SHL),
    .cout(cout), .LD(LD), .Output(AC1_OUT));
endmodule

module _8bit_ALU (
  input  AND,
  input  ADD,
  input  DR,
  input  INP,
  input  COMP,
  input  SHR,
  input  SHL,
  input  AC0_IN,
  input  AC1_IN,
  input  AC2_IN,
  input  AC3_IN,
  input  AC4_IN,
  input  AC5_IN,
  input  AC6_IN,
  input  AC7_IN,
  input  DR0,
  input  DR1,
  input  LD,
  input  DR2,
  input  DR3,
  input  DR4,
  input  DR5,
  input  DR6,
  input  DR7,
  input  AC_I_1,
  input  INPR0,
  input  INPR1,
  input  INPR2,
  input  PREV_IN,
  input  INPR3,
  input  INPR4,
  input  INPR5,
  input  INPR6,
  input  E,
  input  INPR7,
  output AC0_OUT,
  output AC1_OUT,
  output AC2_OUT,
  output AC3_OUT,
  output AC4_OUT,
  output AC5_OUT,
  output AC6_OUT,
  output AC7_OUT,
  output CARRY
);

  wire n2bit_alu_1_cout, n2bit_alu_2_cout, n2bit_alu_3_cout;

  _2bit_ALU u_2bit_alu_1 (
    .AC0_IN(AC0_IN), .AC1_IN(AC1_IN), .DR0_IN(DR0), .DR1_IN(DR1), .INPR0(INPR0), .INPR1(INPR1), .AND(AND),
    .ADD(ADD), .DR(DR), .INP(INP), .COMP(COMP), .SHR(SHR), .SHL(SHL), .E(E), .PREVIOUS_IN(PREV_IN),
    .ACI_1(AC2_IN), .cout(n2bit_alu_1_cout), .AC0_OUT(AC0_OUT), .AC1_OUT(AC1_OUT), .LD(LD));
  _2bit_ALU u_2bit_alu_2 (
    .AC0_IN(AC2_IN), .AC1_IN(AC3_IN), .DR0_IN(DR2), .DR1_IN(DR3), .INPR0(INPR2), .INPR1(INPR3), .AND(AND),
    .ADD(ADD), .DR(DR), .INP(INP), .COMP(COMP), .SHR(SHR), .SHL(SHL), .E(AC1_IN),
    .PREVIOUS_IN(n2bit_alu_1_cout), .ACI_1(AC4_IN), .cout(n2bit_alu_2_cout), .AC0_OUT(AC2_OUT),
    .AC1_OUT(AC3_OUT), .LD(LD));
  _2bit_ALU u_2bit_alu_3 (
    .AC0_IN(AC4_IN), .AC1_IN(AC5_IN), .DR0_IN(DR4), .DR1_IN(DR5), .INPR0(INPR4), .INPR1(INPR5), .AND(AND),
    .ADD(ADD), .DR(DR), .INP(INP), .COMP(COMP), .SHR(SHR), .SHL(SHL), .E(AC2_IN),
    .PREVIOUS_IN(n2bit_alu_2_cout), .ACI_1(AC6_IN), .cout(n2bit_alu_3_cout), .AC0_OUT(AC4_OUT),
    .AC1_OUT(AC5_OUT), .LD(LD));
  _2bit_ALU u_2bit_alu_4 (
    .AC0_IN(AC6_IN), .AC1_IN(AC7_IN), .DR0_IN(DR6), .DR1_IN(DR7), .INPR0(INPR6), .INPR1(INPR7), .AND(AND),
    .ADD(ADD), .DR(DR), .INP(INP), .COMP(COMP), .SHR(SHR), .SHL(SHL), .E(AC5_IN),
    .PREVIOUS_IN(n2bit_alu_3_cout), .ACI_1(AC_I_1), .cout(CARRY), .AC0_OUT(AC6_OUT), .AC1_OUT(AC7_OUT),
    .LD(LD));
endmodule

module _16bit_ALU (
  input  AND,
  input  ADD,
  input  DR,
  input  IN,
  input  COMP,
  input  SHR,
  input  SHL,
  input  [15:0] AC_IN,
  input  LD,
  input  [15:0] DR_IN,
  input  [7:0] INPR,
  input  clock_for_E,
  output [15:0] ac_out,
  output E_carry
);

  wire and_1_out, and_2_out, n8bit_alu_1_carry, n8bit_alu_2_carry, or_1_out, undriven;

  _8bit_ALU u_8bit_alu_1 (
    .AC0_IN(AC_IN[0]), .AC1_IN(AC_IN[1]), .AC2_IN(AC_IN[2]), .AC3_IN(AC_IN[3]), .AC4_IN(AC_IN[4]),
    .AC5_IN(AC_IN[5]), .AC6_IN(AC_IN[6]), .AC7_IN(AC_IN[7]), .DR0(DR_IN[0]), .DR1(DR_IN[1]), .DR2(DR_IN[2]),
    .DR3(DR_IN[3]), .DR4(DR_IN[4]), .DR5(DR_IN[5]), .DR6(DR_IN[6]), .DR7(DR_IN[7]), .AND(AND), .ADD(ADD),
    .DR(DR), .INP(IN), .COMP(COMP), .SHR(SHR), .SHL(SHL), .INPR0(INPR[7]), .INPR1(INPR[6]), .INPR2(INPR[5]),
    .INPR3(INPR[4]), .INPR4(INPR[3]), .INPR5(INPR[2]), .INPR6(INPR[1]), .INPR7(INPR[0]), .E(E_carry),
    .PREV_IN(1'b0), .AC_I_1(AC_IN[8]), .CARRY(n8bit_alu_1_carry), .LD(LD), .AC0_OUT(ac_out[0]),
    .AC1_OUT(ac_out[1]), .AC2_OUT(ac_out[2]), .AC3_OUT(ac_out[3]), .AC4_OUT(ac_out[4]), .AC5_OUT(ac_out[5]),
    .AC6_OUT(ac_out[6]), .AC7_OUT(ac_out[7]));
  and and_1 (and_1_out, AC_IN[15], SHL);
  and and_2 (and_2_out, SHR, AC_IN[0]);
  or or_1 (or_1_out, and_1_out, n8bit_alu_2_carry, and_2_out);
  _8bit_ALU u_8bit_alu_2 (
    .AC0_IN(AC_IN[8]), .AC1_IN(AC_IN[9]), .AC2_IN(AC_IN[10]), .AC3_IN(AC_IN[11]), .AC4_IN(AC_IN[12]),
    .AC5_IN(AC_IN[13]), .AC6_IN(AC_IN[14]), .AC7_IN(AC_IN[15]), .DR0(DR_IN[8]), .DR1(DR_IN[9]),
    .DR2(DR_IN[10]), .DR3(DR_IN[11]), .DR4(DR_IN[12]), .DR5(DR_IN[13]), .DR6(DR_IN[14]), .DR7(DR_IN[15]),
    .AND(AND), .ADD(ADD), .DR(DR), .INP(IN), .COMP(COMP), .SHR(SHR), .SHL(SHL), .INPR0(1'b0), .INPR1(1'b0),
    .INPR2(1'b0), .INPR3(1'b0), .INPR4(1'b0), .INPR5(1'b0), .INPR6(1'b0), .INPR7(1'b0), .E(AC_IN[7]),
    .PREV_IN(n8bit_alu_1_carry), .AC_I_1(E_carry), .CARRY(n8bit_alu_2_carry), .LD(LD), .AC0_OUT(ac_out[8]),
    .AC1_OUT(ac_out[9]), .AC2_OUT(ac_out[10]), .AC3_OUT(ac_out[11]), .AC4_OUT(ac_out[12]),
    .AC5_OUT(ac_out[13]), .AC6_OUT(ac_out[14]), .AC7_OUT(ac_out[15]));
  D_Flip_Flop d_ff_1 (.clk(clock_for_E), .D(or_1_out), .Q(E_carry), .reset(undriven));  // open: Qn, preset, en
endmodule

module BUS (
  input  [11:0] _001,
  input  [2:0] selection,
  input  [11:0] _010,
  input  [15:0] _011,
  input  [15:0] _100,
  input  [15:0] _101,
  input  [15:0] _110,
  input  [15:0] _111,
  output [15:0] \output 
);

  wire [15:12] undriven, undriven_2;

  Multiplexer #(.select(3), .width(16)) multiplexer_1 (
    .in0({16{1'b0}}), .in1({undriven, _001}), .in2({undriven_2, _010}), .in3(_011), .in4(_100), .in5(_101),
    .in6(_110), .in7(_111), .out(\output ), .sel(selection));  // open: en
endmodule

module R_control (
  input  T0,
  input  T1,
  input  T2,
  input  IEN,
  input  FGI,
  input  FGO,
  input  R,
  input  Clock,
  output R_2
);

  wire and_1_out, and_2_out, not_1_out, not_2_out, not_3_out, or_1_out;

  not not_1 (not_1_out, T0);
  not not_2 (not_2_out, T1);
  not not_3 (not_3_out, T2);
  or or_1 (or_1_out, FGI, FGO);
  and and_1 (and_1_out, not_1_out, not_2_out, not_3_out, IEN, or_1_out);
  and and_2 (and_2_out, T2, R);
  J_K_Flip_Flop j_k_ff_1 (.J(and_1_out), .clk(Clock), .K(and_2_out), .Q(R_2));  // open: Qn, preset, en, reset
endmodule

module IEN_control (
  input  p,
  input  B7,
  input  Clock,
  input  B6,
  input  R,
  input  T2,
  output IEN
);

  wire and_1_out, and_2_out, and_3_out, or_1_out;

  and and_1 (and_1_out, p, B7);
  and and_2 (and_2_out, p, B6);
  and and_3 (and_3_out, R, T2);
  or or_1 (or_1_out, and_2_out, and_3_out);
  J_K_Flip_Flop j_k_ff_1 (.J(and_1_out), .clk(Clock), .K(or_1_out), .Q(IEN));  // open: Qn, preset, en, reset
endmodule

module DR_control (
  input  D0,
  input  T4,
  input  D1,
  input  D2,
  input  D6,
  input  T5,
  output LD,
  output INR
);

  wire and_1_out, and_2_out, and_3_out, and_4_out;

  and and_1 (and_1_out, D0, T4);
  and and_2 (and_2_out, D1, T4);
  and and_3 (and_3_out, D2, T4);
  and and_4 (and_4_out, D6, T4);
  and and_5 (INR, D6, T5);
  or or_1 (LD, and_1_out, and_2_out, and_3_out, and_4_out);
endmodule

module pc_control (
  input  D4,
  input  T4,
  input  D5,
  input  T5,
  input  R_prime,
  input  T1,
  input  R,
  input  T2,
  input  D6,
  input  T6,
  input  r_2,
  input  B4,
  input  B3,
  input  B2,
  input  B1,
  input  P,
  input  B9,
  input  B8,
  input  R_3,
  input  T1_2,
  output LD,
  output INR,
  output CLR
);

  wire and_1_out, and_2_out, and_3_out, and_4_out, and_5_out, and_6_out, and_7_out, and_8_out, and_9_out,
       and_10_out, and_11_out;

  and and_1 (and_1_out, D4, T4);
  and and_2 (and_2_out, D5, T5);
  and and_3 (and_3_out, R_prime, T1);
  and and_4 (and_4_out, R, T2);
  and and_5 (and_5_out, D6, T6);
  and and_6 (and_6_out, r_2, B4);
  and and_7 (and_7_out, r_2, B3);
  and and_8 (and_8_out, r_2, B2);
  and and_9 (and_9_out, r_2, B1);
  and and_10 (and_10_out, P, B9);
  and and_11 (and_11_out, P, B8);
  and and_12 (CLR, R_3, T1_2);
  or or_1 (LD, and_1_out, and_2_out);
  or or_2 (INR, and_3_out, and_4_out, and_5_out, and_6_out, and_7_out, and_8_out, and_9_out, and_10_out, and_11_out);
endmodule

module AR_control (
  input  D_prime_7,
  input  I,
  input  T3,
  input  T2,
  input  R,
  input  T0,
  input  D5,
  input  T4,
  output LD,
  output INR,
  output CLR
);

  wire and_1_out, and_2_out, and_3_out, not_1_out;

  not not_1 (not_1_out, R);
  and and_1 (and_1_out, D_prime_7, I, T3);
  and and_2 (and_2_out, T2, not_1_out);
  and and_3 (and_3_out, not_1_out, T0);
  and and_4 (INR, D5, T4);
  and and_5 (CLR, T0, R);
  or or_1 (LD, and_1_out, and_2_out, and_3_out);
endmodule

module IR_drcoder (
  input  [15:0] IR,
  output D0,
  output D1,
  output D2,
  output D3,
  output D4,
  output D5,
  output D6,
  output D7,
  output [11:0] AR,
  output I
);

  Decoder #(.select(3), .enable("false")) decoder_1 (
    .out0(D0), .out1(D1), .out2(D2), .out3(D3), .out4(D4), .out5(D5), .out6(D6), .out7(D7), .sel(IR[14:12]));

  assign AR = IR[11:0];
  assign I = IR[15];
endmodule

module TR_control (
  input  RCOMP,
  input  T1,
  output LD
);

  wire not_1_out;

  not not_1 (not_1_out, RCOMP);
  and and_1 (LD, not_1_out, T1);
endmodule

module IR_control (
  input  RCOMP,
  input  T1,
  output LD
);

  wire not_1_out;

  not not_1 (not_1_out, RCOMP);
  and and_1 (LD, not_1_out, T1);
endmodule

module DR_AC_TR__load__reg (
  input  Load,
  input  INC,
  input  I0,
  input  I1,
  input  I2,
  input  I3,
  input  I4,
  input  I5,
  input  I6,
  input  I7,
  input  I8,
  input  I9,
  input  I10,
  input  I11,
  input  I12,
  input  I13,
  input  I14,
  input  I15,
  input  CLR,
  input  CLOCK,
  output O0,
  output O1,
  output O2,
  output O3,
  output O4,
  output O5,
  output O6,
  output O7,
  output O8,
  output O9,
  output O10,
  output O11,
  output O12,
  output O13,
  output O14,
  output O15
);

  wire and_1_out, and_2_out, and_3_out, and_4_out, and_5_out, and_6_out, and_7_out, and_8_out, and_9_out,
       and_10_out, and_11_out, and_12_out, and_13_out, and_14_out, and_15_out, and_16_out, and_17_out,
       and_18_out, and_19_out, and_20_out, and_21_out, and_22_out, and_23_out, and_24_out, and_25_out,
       and_26_out, and_27_out, and_28_out, and_29_out, and_30_out, and_31_out, and_32_out, and_33_out,
       and_34_out, and_35_out, and_36_out, and_37_out, and_38_out, and_39_out, and_40_out, and_41_out,
       and_42_out, and_43_out, and_44_out, and_45_out, and_46_out, and_47_out, and_48_out, not_1_out,
       not_2_out, not_3_out, not_4_out, not_5_out, not_6_out, not_7_out, not_8_out, not_9_out, not_10_out,
       not_11_out, not_12_out, not_13_out, not_14_out, not_15_out, not_16_out, not_17_out, or_1_out,
       or_2_out, or_3_out, or_4_out, or_5_out, or_6_out, or_7_out, or_8_out, or_9_out, or_10_out, or_11_out,
       or_12_out, or_13_out, or_14_out, or_15_out, or_16_out, or_17_out, or_18_out, or_19_out, or_20_out,
       or_21_out, or_22_out, or_23_out, or_24_out, or_25_out, or_26_out, or_27_out, or_28_out, or_29_out,
       or_30_out, or_31_out, or_32_out;

  not not_1 (not_1_out, I0);
  not not_2 (not_2_out, I1);
  not not_3 (not_3_out, I2);
  not not_4 (not_4_out, I3);
  not not_5 (not_5_out, I4);
  not not_6 (not_6_out, I5);
  not not_7 (not_7_out, I6);
  not not_8 (not_8_out, I7);
  not not_9 (not_9_out, I8);
  not not_10 (not_10_out, I9);
  not not_11 (not_11_out, I10);
  not not_12 (not_12_out, I11);
  not not_13 (not_13_out, I12);
  not not_14 (not_14_out, I13);
  not not_15 (not_15_out, I14);
  not not_16 (not_16_out, I15);
  not not_17 (not_17_out, Load);
  and and_1 (and_1_out, not_17_out, INC);
  and and_2 (and_2_out, Load, I0);
  and and_3 (and_3_out, Load, not_1_out);
  and and_4 (and_4_out, Load, I1);
  and and_5 (and_5_out, and_1_out, O0);
  and and_6 (and_6_out, Load, not_2_out);
  and and_7 (and_7_out, Load, I2);
  and and_8 (and_8_out, and_5_out, O1);
  and and_9 (and_9_out, Load, not_3_out);
  and and_10 (and_10_out, Load, I3);
  and and_11 (and_11_out, Load, not_4_out);
  and and_12 (and_12_out, Load, I4);
  and and_13 (and_13_out, Load, not_5_out);
  and and_14 (and_14_out, Load, I5);
  and and_15 (and_15_out, Load, not_6_out);
  and and_16 (and_16_out, Load, I6);
  and and_17 (and_17_out, Load, not_7_out);
  and and_18 (and_18_out, Load, I7);
  and and_19 (and_19_out, Load, not_8_out);
  and and_20 (and_20_out, Load, I8);
  and and_21 (and_21_out, Load, not_9_out);
  and and_22 (and_22_out, Load, I9);
  and and_23 (and_23_out, Load, not_10_out);
  and and_24 (and_24_out, Load, I10);
  and and_25 (and_25_out, Load, not_11_out);
  and and_26 (and_26_out, Load, I11);
  and and_27 (and_27_out, Load, not_12_out);
  and and_28 (and_28_out, Load, I12);
  and and_29 (and_29_out, Load, not_13_out);
  and and_30 (and_30_out, Load, I13);
  and and_31 (and_31_out, Load, not_14_out);
  and and_32 (and_32_out, Load, I14);
  and and_33 (and_33_out, Load, not_15_out);
  and and_34 (and_34_out, Load, I15);
  and and_35 (and_35_out, Load, not_16_out);
  and and_36 (and_36_out, and_8_out, O2);
  and and_37 (and_37_out, and_36_out, O3);
  and and_38 (and_38_out, and_37_out, O4);
  and and_39 (and_39_out, and_38_out, O5);
  and and_40 (and_40_out, and_39_out, O6);
  and and_41 (and_41_out, and_40_out, O7);
  and and_42 (and_42_out, and_41_out, O8);
  and and_43 (and_43_out, and_42_out, O9);
  and and_44 (and_44_out, and_43_out, O10);
  and and_45 (and_45_out, and_44_out, O11);
  and and_46 (and_46_out, and_45_out, O12);
  and and_47 (and_47_out, and_46_out, O13);
  and and_48 (and_48_out, and_47_out, O14);
  or or_1 (or_1_out, and_1_out, and_2_out);
  or or_2 (or_2_out, and_1_out, and_3_out);
  or or_3 (or_3_out, and_5_out, and_4_out);
  or or_4 (or_4_out, and_5_out, and_6_out);
  or or_5 (or_5_out, and_8_out, and_7_out);
  or or_6 (or_6_out, and_8_out, and_9_out);
  or or_7 (or_7_out, and_36_out, and_10_out);
  or or_8 (or_8_out, and_36_out, and_11_out);
  or or_9 (or_9_out, and_37_out, and_12_out);
  or or_10 (or_10_out, and_37_out, and_13_out);
  or or_11 (or_11_out, and_38_out, and_14_out);
  or or_12 (or_12_out, and_38_out, and_15_out);
  or or_13 (or_13_out, and_39_out, and_16_out);
  or or_14 (or_14_out, and_39_out, and_17_out);
  or or_15 (or_15_out, and_40_out, and_18_out);
  or or_16 (or_16_out, and_40_out, and_19_out);
  or or_17 (or_17_out, and_41_out, and_20_out);
  or or_18 (or_18_out, and_41_out, and_21_out);
  or or_19 (or_19_out, and_42_out, and_22_out);
  or or_20 (or_20_out, and_42_out, and_23_out);
  or or_21 (or_21_out, and_43_out, and_24_out);
  or or_22 (or_22_out, and_43_out, and_25_out);
  or or_23 (or_23_out, and_44_out, and_26_out);
  or or_24 (or_24_out, and_44_out, and_27_out);
  or or_25 (or_25_out, and_45_out, and_28_out);
  or or_26 (or_26_out, and_45_out, and_29_out);
  or or_27 (or_27_out, and_46_out, and_30_out);
  or or_28 (or_28_out, and_46_out, and_31_out);
  or or_29 (or_29_out, and_47_out, and_32_out);
  or or_30 (or_30_out, and_47_out, and_33_out);
  or or_31 (or_31_out, and_48_out, and_34_out);
  or or_32 (or_32_out, and_48_out, and_35_out);
  J_K_Flip_Flop j_k_ff_1 (.J(or_1_out), .clk(CLOCK), .K(or_2_out), .Q(O0), .reset(CLR));  // open: Qn, preset, en
  J_K_Flip_Flop j_k_ff_2 (.J(or_3_out), .clk(CLOCK), .K(or_4_out), .Q(O1), .reset(CLR));  // open: Qn, preset, en
  J_K_Flip_Flop j_k_ff_3 (.J(or_5_out), .clk(CLOCK), .K(or_6_out), .Q(O2), .reset(CLR));  // open: Qn, preset, en
  J_K_Flip_Flop j_k_ff_4 (.J(or_7_out), .clk(CLOCK), .K(or_8_out), .Q(O3), .reset(CLR));  // open: Qn, preset, en
  J_K_Flip_Flop j_k_ff_5 (.J(or_9_out), .clk(CLOCK), .K(or_10_out), .Q(O4), .reset(CLR));  // open: Qn, preset, en
  J_K_Flip_Flop j_k_ff_6 (.J(or_11_out), .clk(CLOCK), .K(or_12_out), .Q(O5), .reset(CLR));  // open: Qn, preset, en
  J_K_Flip_Flop j_k_ff_7 (.J(or_13_out), .clk(CLOCK), .K(or_14_out), .Q(O6), .reset(CLR));  // open: Qn, preset, en
  J_K_Flip_Flop j_k_ff_8 (.J(or_15_out), .clk(CLOCK), .K(or_16_out), .Q(O7), .reset(CLR));  // open: Qn, preset, en
  J_K_Flip_Flop j_k_ff_9 (.J(or_17_out), .clk(CLOCK), .K(or_18_out), .Q(O8), .reset(CLR));  // open: Qn, preset, en
  J_K_Flip_Flop j_k_ff_10 (.J(or_19_out), .clk(CLOCK), .K(or_20_out), .Q(O9), .reset(CLR));  // open: Qn, preset, en
  J_K_Flip_Flop j_k_ff_11 (.J(or_21_out), .clk(CLOCK), .K(or_22_out), .Q(O10), .reset(CLR));  // open: Qn, preset, en
  J_K_Flip_Flop j_k_ff_12 (.J(or_23_out), .clk(CLOCK), .K(or_24_out), .Q(O11), .reset(CLR));  // open: Qn, preset, en
  J_K_Flip_Flop j_k_ff_13 (.J(or_25_out), .clk(CLOCK), .K(or_26_out), .Q(O12), .reset(CLR));  // open: Qn, preset, en
  J_K_Flip_Flop j_k_ff_14 (.J(or_27_out), .clk(CLOCK), .K(or_28_out), .Q(O13), .reset(CLR));  // open: Qn, preset, en
  J_K_Flip_Flop j_k_ff_15 (.J(or_29_out), .clk(CLOCK), .K(or_30_out), .Q(O14), .reset(CLR));  // open: Qn, preset, en
  J_K_Flip_Flop j_k_ff_16 (.J(or_31_out), .clk(CLOCK), .K(or_32_out), .Q(O15), .reset(CLR));  // open: Qn, preset, en
endmodule

module IR__reg (
  input  Load,
  input  I0,
  input  I1,
  input  I2,
  input  I3,
  input  I4,
  input  I5,
  input  I6,
  input  I7,
  input  I8,
  input  I9,
  input  I10,
  input  I11,
  input  I12,
  input  I13,
  input  I14,
  input  I15,
  input  CLOCK,
  output O0,
  output O1,
  output O2,
  output O3,
  output O4,
  output O5,
  output O6,
  output O7,
  output O8,
  output O9,
  output O10,
  output O11,
  output O12,
  output O13,
  output O14,
  output O15
);

  wire and_1_out, and_2_out, and_3_out, and_4_out, and_5_out, and_6_out, and_7_out, and_8_out, and_9_out,
       and_10_out, and_11_out, and_12_out, and_13_out, and_14_out, and_15_out, and_16_out, and_17_out,
       and_18_out, and_19_out, and_20_out, and_21_out, and_22_out, and_23_out, and_24_out, and_25_out,
       and_26_out, and_27_out, and_28_out, and_29_out, and_30_out, and_31_out, and_32_out, not_1_out,
       not_2_out, not_3_out, not_4_out, not_5_out, not_6_out, not_7_out, not_8_out, not_9_out, not_10_out,
       not_11_out, not_12_out, not_13_out, not_14_out, not_15_out, not_16_out, undriven, undriven_2,
       undriven_3, undriven_4, undriven_5, undriven_6, undriven_7, undriven_8, undriven_9, undriven_10,
       undriven_11, undriven_12, undriven_13, undriven_14, undriven_15, undriven_16;

  not not_1 (not_1_out, I0);
  not not_2 (not_2_out, I1);
  not not_3 (not_3_out, I2);
  not not_4 (not_4_out, I3);
  not not_5 (not_5_out, I4);
  not not_6 (not_6_out, I5);
  not not_7 (not_7_out, I6);
  not not_8 (not_8_out, I7);
  not not_9 (not_9_out, I8);
  not not_10 (not_10_out, I9);
  not not_11 (not_11_out, I10);
  not not_12 (not_12_out, I11);
  not not_13 (not_13_out, I12);
  not not_14 (not_14_out, I13);
  not not_15 (not_15_out, I14);
  not not_16 (not_16_out, I15);
  and and_1 (and_1_out, Load, I0);
  and and_2 (and_2_out, Load, not_1_out);
  and and_3 (and_3_out, Load, I1);
  and and_4 (and_4_out, Load, not_2_out);
  and and_5 (and_5_out, Load, I2);
  and and_6 (and_6_out, Load, not_3_out);
  and and_7 (and_7_out, Load, I3);
  and and_8 (and_8_out, Load, not_4_out);
  and and_9 (and_9_out, Load, I4);
  and and_10 (and_10_out, Load, not_5_out);
  and and_11 (and_11_out, Load, I5);
  and and_12 (and_12_out, Load, not_6_out);
  and and_13 (and_13_out, Load, I6);
  and and_14 (and_14_out, Load, not_7_out);
  and and_15 (and_15_out, Load, I7);
  and and_16 (and_16_out, Load, not_8_out);
  and and_17 (and_17_out, Load, I8);
  and and_18 (and_18_out, Load, not_9_out);
  and and_19 (and_19_out, Load, I9);
  and and_20 (and_20_out, Load, not_10_out);
  and and_21 (and_21_out, Load, I10);
  and and_22 (and_22_out, Load, not_11_out);
  and and_23 (and_23_out, Load, I11);
  and and_24 (and_24_out, Load, not_12_out);
  and and_25 (and_25_out, Load, I12);
  and and_26 (and_26_out, Load, not_13_out);
  and and_27 (and_27_out, Load, I13);
  and and_28 (and_28_out, Load, not_14_out);
  and and_29 (and_29_out, Load, I14);
  and and_30 (and_30_out, Load, not_15_out);
  and and_31 (and_31_out, Load, I15);
  and and_32 (and_32_out, Load, not_16_out);
  J_K_Flip_Flop j_k_ff_1 (.J(and_1_out), .clk(CLOCK), .K(and_2_out), .Q(O0), .reset(undriven));  // open: Qn, preset, en
  J_K_Flip_Flop j_k_ff_2 (
    .J(and_3_out), .clk(CLOCK), .K(and_4_out), .Q(O1), .reset(undriven_2));  // open: Qn, preset, en
  J_K_Flip_Flop j_k_ff_3 (
    .J(and_5_out), .clk(CLOCK), .K(and_6_out), .Q(O2), .reset(undriven_3));  // open: Qn, preset, en
  J_K_Flip_Flop j_k_ff_4 (
    .J(and_7_out), .clk(CLOCK), .K(and_8_out), .Q(O3), .reset(undriven_4));  // open: Qn, preset, en
  J_K_Flip_Flop j_k_ff_5 (
    .J(and_9_out), .clk(CLOCK), .K(and_10_out), .Q(O4), .reset(undriven_5));  // open: Qn, preset, en
  J_K_Flip_Flop j_k_ff_6 (
    .J(and_11_out), .clk(CLOCK), .K(and_12_out), .Q(O5), .reset(undriven_6));  // open: Qn, preset, en
  J_K_Flip_Flop j_k_ff_7 (
    .J(and_13_out), .clk(CLOCK), .K(and_14_out), .Q(O6), .reset(undriven_7));  // open: Qn, preset, en
  J_K_Flip_Flop j_k_ff_8 (
    .J(and_15_out), .clk(CLOCK), .K(and_16_out), .Q(O7), .reset(undriven_8));  // open: Qn, preset, en
  J_K_Flip_Flop j_k_ff_9 (
    .J(and_17_out), .clk(CLOCK), .K(and_18_out), .Q(O8), .reset(undriven_9));  // open: Qn, preset, en
  J_K_Flip_Flop j_k_ff_10 (
    .J(and_19_out), .clk(CLOCK), .K(and_20_out), .Q(O9), .reset(undriven_10));  // open: Qn, preset, en
  J_K_Flip_Flop j_k_ff_11 (
    .J(and_21_out), .clk(CLOCK), .K(and_22_out), .Q(O10), .reset(undriven_11));  // open: Qn, preset, en
  J_K_Flip_Flop j_k_ff_12 (
    .J(and_23_out), .clk(CLOCK), .K(and_24_out), .Q(O11), .reset(undriven_12));  // open: Qn, preset, en
  J_K_Flip_Flop j_k_ff_13 (
    .J(and_25_out), .clk(CLOCK), .K(and_26_out), .Q(O12), .reset(undriven_13));  // open: Qn, preset, en
  J_K_Flip_Flop j_k_ff_14 (
    .J(and_27_out), .clk(CLOCK), .K(and_28_out), .Q(O13), .reset(undriven_14));  // open: Qn, preset, en
  J_K_Flip_Flop j_k_ff_15 (
    .J(and_29_out), .clk(CLOCK), .K(and_30_out), .Q(O14), .reset(undriven_15));  // open: Qn, preset, en
  J_K_Flip_Flop j_k_ff_16 (
    .J(and_31_out), .clk(CLOCK), .K(and_32_out), .Q(O15), .reset(undriven_16));  // open: Qn, preset, en
endmodule

module AR_PC__load_reg (
  input  Load,
  input  INC,
  input  I0,
  input  I1,
  input  I2,
  input  I3,
  input  I4,
  input  I5,
  input  I6,
  input  I7,
  input  I8,
  input  I9,
  input  I10,
  input  I11,
  input  CLOCK,
  input  CLR,
  output O0,
  output O1,
  output O2,
  output O3,
  output O4,
  output O5,
  output O6,
  output O7,
  output O8,
  output O9,
  output O10,
  output O11
);

  wire and_1_out, and_2_out, and_3_out, and_4_out, and_5_out, and_6_out, and_7_out, and_8_out, and_9_out,
       and_10_out, and_11_out, and_12_out, and_13_out, and_14_out, and_15_out, and_16_out, and_17_out,
       and_18_out, and_19_out, and_20_out, and_21_out, and_22_out, and_23_out, and_24_out, and_25_out,
       and_26_out, and_27_out, and_28_out, and_29_out, and_30_out, and_31_out, and_32_out, and_33_out,
       and_34_out, and_35_out, and_36_out, not_1_out, not_2_out, not_3_out, not_4_out, not_5_out, not_6_out,
       not_7_out, not_8_out, not_9_out, not_10_out, not_11_out, not_12_out, not_13_out, or_1_out, or_2_out,
       or_3_out, or_4_out, or_5_out, or_6_out, or_7_out, or_8_out, or_9_out, or_10_out, or_11_out, or_12_out,
       or_13_out, or_14_out, or_15_out, or_16_out, or_17_out, or_18_out, or_19_out, or_20_out, or_21_out,
       or_22_out, or_23_out, or_24_out;

  not not_1 (not_1_out, I0);
  not not_2 (not_2_out, I1);
  not not_3 (not_3_out, I2);
  not not_4 (not_4_out, I3);
  not not_5 (not_5_out, I4);
  not not_6 (not_6_out, I5);
  not not_7 (not_7_out, I6);
  not not_8 (not_8_out, I7);
  not not_9 (not_9_out, I8);
  not not_10 (not_10_out, I9);
  not not_11 (not_11_out, I10);
  not not_12 (not_12_out, I11);
  not not_13 (not_13_out, Load);
  and and_1 (and_1_out, not_13_out, INC);
  and and_2 (and_2_out, Load, I0);
  and and_3 (and_3_out, Load, not_1_out);
  and and_4 (and_4_out, Load, I1);
  and and_5 (and_5_out, and_1_out, O0);
  and and_6 (and_6_out, Load, not_2_out);
  and and_7 (and_7_out, Load, I2);
  and and_8 (and_8_out, Load, not_3_out);
  and and_9 (and_9_out, Load, I3);
  and and_10 (and_10_out, Load, not_4_out);
  and and_11 (and_11_out, Load, I4);
  and and_12 (and_12_out, Load, not_5_out);
  and and_13 (and_13_out, Load, I5);
  and and_14 (and_14_out, Load, not_6_out);
  and and_15 (and_15_out, Load, I6);
  and and_16 (and_16_out, Load, not_7_out);
  and and_17 (and_17_out, Load, I7);
  and and_18 (and_18_out, Load, not_8_out);
  and and_19 (and_19_out, Load, I8);
  and and_20 (and_20_out, Load, not_9_out);
  and and_21 (and_21_out, Load, I9);
  and and_22 (and_22_out, Load, not_10_out);
  and and_23 (and_23_out, Load, I10);
  and and_24 (and_24_out, Load, not_11_out);
  and and_25 (and_25_out, Load, I11);
  and and_26 (and_26_out, Load, not_12_out);
  and and_27 (and_27_out, and_5_out, O1);
  and and_28 (and_28_out, and_27_out, O2);
  and and_29 (and_29_out, and_28_out, O3);
  and and_30 (and_30_out, and_29_out, O4);
  and and_31 (and_31_out, and_30_out, O5);
  and and_32 (and_32_out, and_31_out, O6);
  and and_33 (and_33_out, and_32_out, O7);
  and and_34 (and_34_out, and_33_out, O8);
  and and_35 (and_35_out, and_34_out, O9);
  and and_36 (and_36_out, and_35_out, O10);
  or or_1 (or_1_out, and_1_out, and_2_out);
  or or_2 (or_2_out, and_1_out, and_3_out);
  or or_3 (or_3_out, and_5_out, and_4_out);
  or or_4 (or_4_out, and_5_out, and_6_out);
  or or_5 (or_5_out, and_27_out, and_7_out);
  or or_6 (or_6_out, and_27_out, and_8_out);
  or or_7 (or_7_out, and_28_out, and_9_out);
  or or_8 (or_8_out, and_28_out, and_10_out);
  or or_9 (or_9_out, and_29_out, and_11_out);
  or or_10 (or_10_out, and_29_out, and_12_out);
  or or_11 (or_11_out, and_30_out, and_13_out);
  or or_12 (or_12_out, and_30_out, and_14_out);
  or or_13 (or_13_out, and_31_out, and_15_out);
  or or_14 (or_14_out, and_31_out, and_16_out);
  or or_15 (or_15_out, and_32_out, and_17_out);
  or or_16 (or_16_out, and_32_out, and_18_out);
  or or_17 (or_17_out, and_33_out, and_19_out);
  or or_18 (or_18_out, and_33_out, and_20_out);
  or or_19 (or_19_out, and_34_out, and_21_out);
  or or_20 (or_20_out, and_34_out, and_22_out);
  or or_21 (or_21_out, and_35_out, and_23_out);
  or or_22 (or_22_out, and_35_out, and_24_out);
  or or_23 (or_23_out, and_36_out, and_25_out);
  or or_24 (or_24_out, and_36_out, and_26_out);
  J_K_Flip_Flop j_k_ff_1 (.J(or_1_out), .clk(CLOCK), .K(or_2_out), .Q(O0), .reset(CLR));  // open: Qn, preset, en
  J_K_Flip_Flop j_k_ff_2 (.J(or_3_out), .clk(CLOCK), .K(or_4_out), .Q(O1), .reset(CLR));  // open: Qn, preset, en
  J_K_Flip_Flop j_k_ff_3 (.J(or_5_out), .clk(CLOCK), .K(or_6_out), .Q(O2), .reset(CLR));  // open: Qn, preset, en
  J_K_Flip_Flop j_k_ff_4 (.J(or_7_out), .clk(CLOCK), .K(or_8_out), .Q(O3), .reset(CLR));  // open: Qn, preset, en
  J_K_Flip_Flop j_k_ff_5 (.J(or_9_out), .clk(CLOCK), .K(or_10_out), .Q(O4), .reset(CLR));  // open: Qn, preset, en
  J_K_Flip_Flop j_k_ff_6 (.J(or_11_out), .clk(CLOCK), .K(or_12_out), .Q(O5), .reset(CLR));  // open: Qn, preset, en
  J_K_Flip_Flop j_k_ff_7 (.J(or_13_out), .clk(CLOCK), .K(or_14_out), .Q(O6), .reset(CLR));  // open: Qn, preset, en
  J_K_Flip_Flop j_k_ff_8 (.J(or_15_out), .clk(CLOCK), .K(or_16_out), .Q(O7), .reset(CLR));  // open: Qn, preset, en
  J_K_Flip_Flop j_k_ff_9 (.J(or_17_out), .clk(CLOCK), .K(or_18_out), .Q(O8), .reset(CLR));  // open: Qn, preset, en
  J_K_Flip_Flop j_k_ff_10 (.J(or_19_out), .clk(CLOCK), .K(or_20_out), .Q(O9), .reset(CLR));  // open: Qn, preset, en
  J_K_Flip_Flop j_k_ff_11 (.J(or_21_out), .clk(CLOCK), .K(or_22_out), .Q(O10), .reset(CLR));  // open: Qn, preset, en
  J_K_Flip_Flop j_k_ff_12 (.J(or_23_out), .clk(CLOCK), .K(or_24_out), .Q(O11), .reset(CLR));  // open: Qn, preset, en
endmodule

module OUTR__load_reg (
  input  Load,
  input  I0,
  input  I1,
  input  I2,
  input  I3,
  input  I4,
  input  I5,
  input  I6,
  input  I7,
  input  CLOCK,
  output O0,
  output O1,
  output O2,
  output O3,
  output O4,
  output O5,
  output O6,
  output O7
);

  wire and_1_out, and_2_out, and_3_out, and_4_out, and_5_out, and_6_out, and_7_out, and_8_out, and_9_out,
       and_10_out, and_11_out, and_12_out, and_13_out, and_14_out, and_15_out, and_16_out, not_1_out,
       not_2_out, not_3_out, not_4_out, not_5_out, not_6_out, not_7_out, not_8_out, undriven, undriven_2,
       undriven_3, undriven_4, undriven_5, undriven_6, undriven_7, undriven_8;

  not not_1 (not_1_out, I0);
  not not_2 (not_2_out, I1);
  not not_3 (not_3_out, I2);
  not not_4 (not_4_out, I3);
  not not_5 (not_5_out, I4);
  not not_6 (not_6_out, I5);
  not not_7 (not_7_out, I6);
  not not_8 (not_8_out, I7);
  and and_1 (and_1_out, Load, I0);
  and and_2 (and_2_out, Load, not_1_out);
  and and_3 (and_3_out, Load, I1);
  and and_4 (and_4_out, Load, not_2_out);
  and and_5 (and_5_out, Load, I2);
  and and_6 (and_6_out, Load, not_3_out);
  and and_7 (and_7_out, Load, I3);
  and and_8 (and_8_out, Load, not_4_out);
  and and_9 (and_9_out, Load, I4);
  and and_10 (and_10_out, Load, not_5_out);
  and and_11 (and_11_out, Load, I5);
  and and_12 (and_12_out, Load, not_6_out);
  and and_13 (and_13_out, Load, I6);
  and and_14 (and_14_out, Load, not_7_out);
  and and_15 (and_15_out, Load, I7);
  and and_16 (and_16_out, Load, not_8_out);
  J_K_Flip_Flop j_k_ff_1 (.J(and_1_out), .clk(CLOCK), .K(and_2_out), .Q(O0), .reset(undriven));  // open: Qn, preset, en
  J_K_Flip_Flop j_k_ff_2 (
    .J(and_3_out), .clk(CLOCK), .K(and_4_out), .Q(O1), .reset(undriven_2));  // open: Qn, preset, en
  J_K_Flip_Flop j_k_ff_3 (
    .J(and_5_out), .clk(CLOCK), .K(and_6_out), .Q(O2), .reset(undriven_3));  // open: Qn, preset, en
  J_K_Flip_Flop j_k_ff_4 (
    .J(and_7_out), .clk(CLOCK), .K(and_8_out), .Q(O3), .reset(undriven_4));  // open: Qn, preset, en
  J_K_Flip_Flop j_k_ff_5 (
    .J(and_9_out), .clk(CLOCK), .K(and_10_out), .Q(O4), .reset(undriven_5));  // open: Qn, preset, en
  J_K_Flip_Flop j_k_ff_6 (
    .J(and_11_out), .clk(CLOCK), .K(and_12_out), .Q(O5), .reset(undriven_6));  // open: Qn, preset, en
  J_K_Flip_Flop j_k_ff_7 (
    .J(and_13_out), .clk(CLOCK), .K(and_14_out), .Q(O6), .reset(undriven_7));  // open: Qn, preset, en
  J_K_Flip_Flop j_k_ff_8 (
    .J(and_15_out), .clk(CLOCK), .K(and_16_out), .Q(O7), .reset(undriven_8));  // open: Qn, preset, en
endmodule

module INPR__reg (
  input  I0,
  input  I1,
  input  I2,
  input  I3,
  input  I4,
  input  I5,
  input  I6,
  input  I7,
  input  CLOCK,
  output O0,
  output O1,
  output O2,
  output O3,
  output O4,
  output O5,
  output O6,
  output O7
);

  wire not_1_out, not_2_out, not_3_out, not_4_out, not_5_out, not_6_out, not_7_out, not_8_out;

  not not_1 (not_1_out, I0);
  not not_2 (not_2_out, I1);
  not not_3 (not_3_out, I2);
  not not_4 (not_4_out, I3);
  not not_5 (not_5_out, I4);
  not not_6 (not_6_out, I5);
  not not_7 (not_7_out, I6);
  not not_8 (not_8_out, I7);
  J_K_Flip_Flop j_k_ff_1 (.J(I0), .clk(CLOCK), .K(not_1_out), .Q(O0));  // open: Qn, preset, en, reset
  J_K_Flip_Flop j_k_ff_2 (.J(I1), .clk(CLOCK), .K(not_2_out), .Q(O1));  // open: Qn, preset, en, reset
  J_K_Flip_Flop j_k_ff_3 (.J(I2), .clk(CLOCK), .K(not_3_out), .Q(O2));  // open: Qn, preset, en, reset
  J_K_Flip_Flop j_k_ff_4 (.J(I3), .clk(CLOCK), .K(not_4_out), .Q(O3));  // open: Qn, preset, en, reset
  J_K_Flip_Flop j_k_ff_5 (.J(I4), .clk(CLOCK), .K(not_5_out), .Q(O4));  // open: Qn, preset, en, reset
  J_K_Flip_Flop j_k_ff_6 (.J(I5), .clk(CLOCK), .K(not_6_out), .Q(O5));  // open: Qn, preset, en, reset
  J_K_Flip_Flop j_k_ff_7 (.J(I6), .clk(CLOCK), .K(not_7_out), .Q(O6));  // open: Qn, preset, en, reset
  J_K_Flip_Flop j_k_ff_8 (.J(I7), .clk(CLOCK), .K(not_8_out), .Q(O7));  // open: Qn, preset, en, reset
endmodule

module memory_control (
  input  D0,
  input  D1,
  input  D2,
  input  D3,
  input  D4,
  input  D5,
  input  D6,
  input  D7,
  input  I,
  input  R,
  input  T1,
  input  T4,
  input  T3,
  input  T6,
  output Write,
  output Read
);

  wire and_1_out, and_2_out, and_3_out, and_4_out, and_5_out, and_6_out, and_7_out, and_8_out, and_9_out,
       and_10_out, not_1_out, not_2_out;

  not not_1 (not_1_out, D7);
  not not_2 (not_2_out, R);
  and and_1 (and_1_out, R, T1);
  and and_2 (and_2_out, D3, T4);
  and and_3 (and_3_out, D5, T4);
  and and_4 (and_4_out, D6, T6);
  and and_5 (and_5_out, not_2_out, T1);
  and and_6 (and_6_out, not_1_out, I, T3);
  and and_7 (and_7_out, D0, T4);
  and and_8 (and_8_out, D1, T4);
  and and_9 (and_9_out, D2, T4);
  and and_10 (and_10_out, D6, T4);
  or or_1 (Write, and_1_out, and_2_out, and_3_out, and_4_out);
  or or_2 (Read, and_5_out, and_6_out, and_7_out, and_8_out, and_9_out, and_10_out);
endmodule
